# Fritzing sketch setup (saved by Fritzing 0.9.3b)
breadboards: 1

parts:
  R1 = Resistor [tolerance=±5% resistance=220 package=THT]  # not connected
  Part1 = Arduino Uno (Rev3)
  LED1 = LED - 5mm [color="Red (633nm)" package="5 mm [THT]"]
  J1 = Infrared Proximity Sensor

nets:
  N1: Part1.D13/SCK, LED1.anode
  GND: Part1.GND, J1.GND
  5V: Part1.5V, J1.Vcc
